# Fritzing sketch roboRIO MTX (saved by Fritzing 0.9.0b)
circuit board: 10.7679cm x 7.06578cm
breadboards: 1

parts:
  DIO_0 = male pin header, 3 pins [form="♂ (male)"]
  DIO_1 = male pin header, 3 pins [form="♂ (male)"]
  DIO_2 = male pin header, 3 pins [form="♂ (male)"]
  DIO_3 = male pin header, 3 pins [form="♂ (male)"]
  DIO_4 = male pin header, 3 pins [form="♂ (male)"]
  DIO_5 = male pin header, 3 pins [form="♂ (male)"]
  DIO_6 = male pin header, 3 pins [form="♂ (male)"]
  DIO_7 = male pin header, 3 pins [form="♂ (male)"]
  DIO_8 = male pin header, 3 pins [form="♂ (male)"]
  DIO_9 = male pin header, 3 pins [form="♂ (male)"]
  DIO_10 = male pin header, 3 pins [form="♂ (male)"]
  DIO_11 = male pin header, 3 pins [form="♂ (male)"]
  DIO_12 = male pin header, 3 pins [form="♂ (male)"]
  DIO_13 = male pin header, 3 pins [form="♂ (male)"]
  DIO_14 = male pin header, 3 pins [form="♂ (male)"]
  DIO_15 = male pin header, 3 pins [form="♂ (male)"]
  I2C = male pin header, 4 pins [form="♂ (male)"]
  roboRIO_MTX = shrouded pin header, 34 pins [form="♂ (shrouded male)"]
  RS232 = male pin header, 3 pins [form="♂ (male)"]
  PWM_0 = male pin header, 3 pins [form="♂ (male)"]
  PWM_1 = male pin header, 3 pins [form="♂ (male)"]
  PWM_2 = male pin header, 3 pins [form="♂ (male)"]
  PWM_3 = male pin header, 3 pins [form="♂ (male)"]
  PWM_4 = male pin header, 3 pins [form="♂ (male)"]
  PWM_5 = male pin header, 3 pins [form="♂ (male)"]
  PWM_6 = male pin header, 3 pins [form="♂ (male)"]
  PWM_7 = male pin header, 3 pins [form="♂ (male)"]
  PWM_8 = male pin header, 3 pins [form="♂ (male)"]
  PWM_9 = male pin header, 3 pins [form="♂ (male)"]
  AI_0 = male pin header, 3 pins [form="♂ (male)"]
  AI_1 = male pin header, 3 pins [form="♂ (male)"]
  AO_1 = male pin header, 3 pins [form="♂ (male)"]
  AO_0 = male pin header, 3 pins [form="♂ (male)"]
  AO_2 = male pin header, 3 pins [form="♂ (male)"]
  AO_3 = male pin header, 3 pins [form="♂ (male)"]
  LED1 = LED - 5mm [color="Red (633nm)" package="5 mm [THT]"]
  R1 = Resistor [tolerance=±5% resistance=330 package=THT]

nets:
  N1: DIO_0.pin1, DIO_1.pin1, DIO_2.pin1, DIO_3.pin1, DIO_4.pin1, DIO_5.pin1, DIO_6.pin1, DIO_7.pin1, DIO_8.pin1, DIO_9.pin1, DIO_10.pin1, DIO_11.pin1, DIO_12.pin1, DIO_13.pin1, DIO_14.pin1, DIO_15.pin1, I2C.pin1, roboRIO_MTX.pin20, PWM_0.pin3, PWM_1.pin3, PWM_2.pin3, PWM_3.pin3, PWM_4.pin3, PWM_5.pin3, PWM_6.pin3, PWM_7.pin3, PWM_8.pin3, PWM_9.pin3, R1.Pin_1
  N2: DIO_0.pin2, DIO_1.pin2, DIO_2.pin2, DIO_3.pin2, DIO_4.pin2, DIO_5.pin2, DIO_6.pin2, DIO_7.pin2, DIO_8.pin2, DIO_9.pin2, DIO_10.pin2, DIO_11.pin2, DIO_12.pin2, DIO_13.pin2, DIO_14.pin2, DIO_15.pin2, I2C.pin2, AO_1.pin2, AO_0.pin2, AO_2.pin2, AO_3.pin2, LED1.anode
  N3: DIO_0.pin3, roboRIO_MTX.pin6, PWM_0.pin1
  N4: DIO_1.pin3, roboRIO_MTX.pin7, PWM_1.pin1
  N5: DIO_2.pin3, roboRIO_MTX.pin8, PWM_2.pin1
  N6: DIO_3.pin3, roboRIO_MTX.pin9, PWM_3.pin1
  N7: DIO_4.pin3, roboRIO_MTX.pin10
  N8: DIO_5.pin3, roboRIO_MTX.pin11
  N9: DIO_6.pin3, roboRIO_MTX.pin12
  N10: DIO_7.pin3, roboRIO_MTX.pin13
  N11: DIO_8.pin3, roboRIO_MTX.pin14, PWM_4.pin1
  N12: DIO_9.pin3, roboRIO_MTX.pin15, PWM_5.pin1
  N13: DIO_10.pin3, roboRIO_MTX.pin16, PWM_6.pin1
  N14: DIO_11.pin3, roboRIO_MTX.pin26, PWM_7.pin1
  N15: DIO_12.pin3, roboRIO_MTX.pin24, PWM_8.pin1
  N16: DIO_13.pin3, roboRIO_MTX.pin22, PWM_9.pin1
  N17: DIO_14.pin3, I2C.pin3, roboRIO_MTX.pin19
  N18: DIO_15.pin3, I2C.pin4, roboRIO_MTX.pin18
  N19: roboRIO_MTX.pin1, PWM_0.pin2, PWM_1.pin2, PWM_2.pin2, PWM_3.pin2, PWM_4.pin2, PWM_5.pin2, PWM_6.pin2, PWM_7.pin2, PWM_8.pin2, PWM_9.pin2, AI_0.pin2, AI_1.pin2
  N20: roboRIO_MTX.pin2, AO_0.pin3
  N21: roboRIO_MTX.pin3, AO_1.pin3
  N22: roboRIO_MTX.pin4, AO_2.pin3
  N23: roboRIO_MTX.pin5, AO_3.pin3
  N24: roboRIO_MTX.pin28, RS232.pin1
  N25: roboRIO_MTX.pin30, RS232.pin2
  N26: roboRIO_MTX.pin31, RS232.pin3
  N27: roboRIO_MTX.pin32, AI_0.pin3, AI_1.pin3, AO_1.pin1, AO_0.pin1, AO_2.pin1, AO_3.pin1
  N28: roboRIO_MTX.pin33, AI_1.pin1
  N29: roboRIO_MTX.pin34, AI_0.pin1
  N30: LED1.cathode, R1.Pin_0

notes:
  FRC 2832: Livonia Warriors
  v0.1 - 14 Sept 2014
