# Fritzing sketch roboRIO MXP (saved by Fritzing 0.9.0b)
circuit board: 10.7679cm x 7.06578cm
breadboards: 1

parts:
  DIO_0 = male pin header, 3 pins [form="♂ (male)"]
  DIO_1 = male pin header, 3 pins [form="♂ (male)"]
  DIO_2 = male pin header, 3 pins [form="♂ (male)"]
  DIO_3 = male pin header, 3 pins [form="♂ (male)"]
  DIO_4 = male pin header, 3 pins [form="♂ (male)"]
  DIO_5 = male pin header, 3 pins [form="♂ (male)"]
  DIO_6 = male pin header, 3 pins [form="♂ (male)"]
  DIO_7 = male pin header, 3 pins [form="♂ (male)"]
  DIO_8 = male pin header, 3 pins [form="♂ (male)"]
  DIO_9 = male pin header, 3 pins [form="♂ (male)"]
  DIO_10 = male pin header, 3 pins [form="♂ (male)"]
  DIO_11 = male pin header, 3 pins [form="♂ (male)"]
  DIO_12 = male pin header, 3 pins [form="♂ (male)"]
  DIO_13 = male pin header, 3 pins [form="♂ (male)"]
  DIO_14 = male pin header, 3 pins [form="♂ (male)"]
  DIO_15 = male pin header, 3 pins [form="♂ (male)"]
  I2C = male pin header, 4 pins [form="♂ (male)"]
  roboRIO_MXP = shrouded pin header, 34 pins [form="♂ (shrouded male)"]
  PWM_0 = male pin header, 3 pins [form="♂ (male)"]
  PWM_1 = male pin header, 3 pins [form="♂ (male)"]
  PWM_2 = male pin header, 3 pins [form="♂ (male)"]
  PWM_3 = male pin header, 3 pins [form="♂ (male)"]
  PWM_4 = male pin header, 3 pins [form="♂ (male)"]
  PWM_5 = male pin header, 3 pins [form="♂ (male)"]
  PWM_6 = male pin header, 3 pins [form="♂ (male)"]
  PWM_7 = male pin header, 3 pins [form="♂ (male)"]
  PWM_8 = male pin header, 3 pins [form="♂ (male)"]
  PWM_9 = male pin header, 3 pins [form="♂ (male)"]
  AO_0 = male pin header, 3 pins [form="♂ (male)"]
  AO_1 = male pin header, 3 pins [form="♂ (male)"]
  AI_1 = male pin header, 3 pins [form="♂ (male)"]
  AI_0 = male pin header, 3 pins [form="♂ (male)"]
  AI_2 = male pin header, 3 pins [form="♂ (male)"]
  AI_3 = male pin header, 3 pins [form="♂ (male)"]
  LED1 = LED - 5mm [color="Red (633nm)" package="5 mm [THT]"]
  R1 = Resistor [tolerance=±5% resistance=330 package=THT]
  Rx/Tx = male pin header, 3 pins [form="♂ (male)"]
  GND = male pin header, 1 pin [form="♂ (male)"]

nets:
  N1: DIO_0.pin1, DIO_1.pin1, DIO_2.pin1, DIO_3.pin1, DIO_4.pin1, DIO_5.pin1, DIO_6.pin1, DIO_7.pin1, DIO_8.pin1, DIO_9.pin1, DIO_10.pin1, DIO_11.pin1, DIO_12.pin1, DIO_13.pin1, DIO_14.pin1, DIO_15.pin1, I2C.pin1, roboRIO_MXP.pin20, PWM_0.pin3, PWM_1.pin3, PWM_2.pin3, PWM_3.pin3, PWM_4.pin3, PWM_5.pin3, PWM_6.pin3, PWM_7.pin3, PWM_8.pin3, PWM_9.pin3, R1.Pin_1, GND.pin1
  N2: DIO_0.pin2, DIO_1.pin2, DIO_2.pin2, DIO_3.pin2, DIO_4.pin2, DIO_5.pin2, DIO_6.pin2, DIO_7.pin2, DIO_8.pin2, DIO_9.pin2, DIO_10.pin2, DIO_11.pin2, DIO_12.pin2, DIO_13.pin2, DIO_14.pin2, DIO_15.pin2, I2C.pin2, roboRIO_MXP.pin1, PWM_0.pin2, PWM_1.pin2, PWM_2.pin2, PWM_3.pin2, PWM_4.pin2, PWM_5.pin2, PWM_6.pin2, PWM_7.pin2, PWM_8.pin2, PWM_9.pin2, AO_0.pin2, AO_1.pin2, AI_1.pin2, AI_0.pin2, AI_2.pin2, AI_3.pin2, LED1.anode
  N3: DIO_0.pin3, roboRIO_MXP.pin6, PWM_0.pin1
  N4: DIO_1.pin3, roboRIO_MXP.pin7, PWM_1.pin1
  N5: DIO_2.pin3, roboRIO_MXP.pin8, PWM_2.pin1
  N6: DIO_3.pin3, roboRIO_MXP.pin9, PWM_3.pin1
  N7: DIO_4.pin3, roboRIO_MXP.pin10
  N8: DIO_5.pin3, roboRIO_MXP.pin11
  N9: DIO_6.pin3, roboRIO_MXP.pin12
  N10: DIO_7.pin3, roboRIO_MXP.pin13
  N11: DIO_8.pin3, roboRIO_MXP.pin14, PWM_4.pin1
  N12: DIO_9.pin3, roboRIO_MXP.pin15, PWM_5.pin1
  N13: DIO_10.pin3, roboRIO_MXP.pin16, PWM_6.pin1
  N14: DIO_11.pin3, roboRIO_MXP.pin26, PWM_7.pin1
  N15: DIO_12.pin3, roboRIO_MXP.pin24, PWM_8.pin1
  N16: DIO_13.pin3, roboRIO_MXP.pin22, PWM_9.pin1
  N17: DIO_14.pin3, I2C.pin3, roboRIO_MXP.pin19
  N18: DIO_15.pin3, I2C.pin4, roboRIO_MXP.pin18
  N19: roboRIO_MXP.pin2, AI_0.pin3
  N20: roboRIO_MXP.pin3, AI_1.pin3
  N21: roboRIO_MXP.pin4, AI_2.pin3
  N22: roboRIO_MXP.pin5, AI_3.pin3
  N23: roboRIO_MXP.pin28, Rx/Tx.pin1
  N24: roboRIO_MXP.pin30, Rx/Tx.pin2
  N25: roboRIO_MXP.pin31, Rx/Tx.pin3
  N26: roboRIO_MXP.pin32, AO_0.pin3, AO_1.pin3, AI_1.pin1, AI_0.pin1, AI_2.pin1, AI_3.pin1
  N27: roboRIO_MXP.pin33, AO_1.pin1
  N28: roboRIO_MXP.pin34, AO_0.pin1
  N29: LED1.cathode, R1.Pin_0

notes:
  FRC 2832: Livonia Warriors
  2014 Oct 27
